# Fritzing sketch schematic (saved by Fritzing 0.9.3b)

parts:
  Raspberry_Pi1 = Raspberry Pi 2
  RELAY1 = CAR RELAY [part_number=NVF4-2 package=THT]
  Q1 = NPN-Transistor [package="TO92 [THT]"]
  R1 = Resistor [tolerance=±5% resistance=220 package="2010 [SMD]"]
  D1 = Rectifier Diode [part_number=1N4001 package="300 mil [THT]"]
  U1 = Voltage Regulator - 5V [package="TO220 [THT]"]
  C1 = Capacitor Polarized [package=nippon_f80]

nets:
  GND: Raspberry_Pi1.GND, Q1.E, U1.GND, C1.-
  N1: Raspberry_Pi1.GPIO25, R1.Pin_0
  N2: Raspberry_Pi1.5V, U1.output_voltage
  12V: RELAY1.85, D1.cathode, U1.input_voltage, C1.+
  N3: RELAY1.86, Q1.C
  N4: Q1.B, R1.Pin_1
